// Logisim project ex2.circ as structural Verilog: 1 circuit, main circuit compute_BrUn
module compute_BrUn (
  input  [31:0] INSTRUCTION,
  output BrUn
);

  wire and_1_out, and_2_out, and_3_out, and_4_out, bit_extender_1_out, not_1_out, not_2_out;
  wire [7:0] xnor_1_out;

  assign xnor_1_out = ~(8'h63 ^ INSTRUCTION[7:0]);  // XNOR_Gate xnor_1, 8 bits wide
  not not_1 (not_1_out, INSTRUCTION[13]);
  and and_1 (and_1_out, not_1_out, INSTRUCTION[14]);
  and and_2 (and_2_out, INSTRUCTION[13], INSTRUCTION[14]);
  Bit_Extender #(.out_width(1)) bit_extender_1 (.in(xnor_1_out), .out(bit_extender_1_out));
  not not_2 (not_2_out, and_1_out);
  and and_3 (and_3_out, bit_extender_1_out, and_2_out);
  and and_4 (and_4_out, not_2_out, bit_extender_1_out);
  or or_1 (BrUn, and_3_out, and_4_out);
endmodule
