// Logisim project control-logic.circ as structural Verilog: 1 circuit, main circuit control_logic
module control_logic (
  input  [31:0] Instruction,
  input  BrEq,
  input  BrLt,
  output PCSel,
  output RegWEn,
  output [2:0] ImmSel,
  output BrUn,
  output ASel,
  output BSel,
  output [3:0] ALUSel,
  output MemWEn,
  output [1:0] WBSel
);

  wire and_1_out, and_2_out, and_3_out, and_4_out, and_5_out, and_6_out, comparator_1_eq, comparator_2_eq,
       comparator_3_eq, comparator_4_eq, comparator_5_eq, comparator_6_eq, comparator_7_eq, comparator_8_eq,
       comparator_9_eq, comparator_10_eq, comparator_10_gt, comparator_10_lt, comparator_11_eq,
       comparator_11_gt, comparator_11_lt, comparator_12_eq, comparator_13_eq, comparator_14_eq,
       comparator_15_eq, comparator_16_eq, comparator_17_eq, comparator_18_eq, comparator_19_eq,
       comparator_20_eq, comparator_21_eq, not_1_out, not_2_out, not_3_out, or_1_out, or_2_out;
  wire [1:0] priority_encoder_2_out, priority_encoder_3_out;
  wire [3:0] typeop;
  wire [5:0] adder_1_out, B11000, bit_extender_1_out, bit_extender_2_out, I00000, I00100, multiplexer_3_out,
       multiplexer_4_out, R01100, ROMInput, S01000;
  wire [15:14] rom_1_data;

  ROM #(.addrWidth(6), .dataWidth(16)) rom_1 (
    .addr(ROMInput), .data({rom_1_data, WBSel, MemWEn, ALUSel, BSel, ASel, BrUn, ImmSel, RegWEn}));
  Comparator #(.mode("unsigned"), .width(5)) comparator_1 (
    .a(Instruction[6:2]), .b(5'b01100), .eq(comparator_1_eq));  // open: gt, lt
  Comparator #(.mode("unsigned"), .width(5)) comparator_2 (
    .a(Instruction[6:2]), .b({5{1'b0}}), .eq(comparator_2_eq));  // open: gt, lt
  Comparator #(.mode("unsigned"), .width(5)) comparator_3 (
    .a(Instruction[6:2]), .b(5'b00100), .eq(comparator_3_eq));  // open: gt, lt
  Comparator #(.mode("unsigned"), .width(5)) comparator_4 (
    .a(Instruction[6:2]), .b(5'b01000), .eq(comparator_4_eq));  // open: gt, lt
  Comparator #(.mode("unsigned"), .width(5)) comparator_5 (
    .a(Instruction[6:2]), .b(5'b11000), .eq(comparator_5_eq));  // open: gt, lt
  Comparator #(.mode("unsigned"), .width(5)) comparator_6 (
    .a(Instruction[6:2]), .b(5'b00101), .eq(comparator_6_eq));  // open: gt, lt
  Comparator #(.mode("unsigned"), .width(5)) comparator_7 (
    .a(Instruction[6:2]), .b(5'b01101), .eq(comparator_7_eq));  // open: gt, lt
  Comparator #(.mode("unsigned"), .width(5)) comparator_8 (
    .a(Instruction[6:2]), .b(5'b11011), .eq(comparator_8_eq));  // open: gt, lt
  Comparator #(.mode("unsigned"), .width(5)) comparator_9 (
    .a(Instruction[6:2]), .b(5'b11001), .eq(comparator_9_eq));  // open: gt, lt
  Multiplexer #(.select(4), .width(6)) multiplexer_1 (
    .in0(R01100), .in1(I00000), .in2(I00100), .in3(S01000), .in4(B11000), .in5(6'b100000), .in6(6'b100001),
    .in7(6'b100010), .in8(6'b100011), .out(ROMInput), .sel(typeop));  // open: in9, in10, in11, in12, in13, in14, in15
  Priority_Encoder #(.select_enc(4)) priority_encoder_1 (
    .in0(comparator_1_eq), .in1(comparator_2_eq), .in2(comparator_3_eq), .in3(comparator_4_eq),
    .in4(comparator_5_eq), .in5(comparator_6_eq), .in6(comparator_7_eq), .in7(comparator_8_eq),
    .in8(comparator_9_eq), .out(typeop));  // open: in9, in10, in11, in12, in13, in14, in15, gs, en_out, en_in
  Comparator #(.width(7)) comparator_10 (
    .a(Instruction[31:25]), .b(7'b0000001), .gt(comparator_10_gt), .eq(comparator_10_eq),
    .lt(comparator_10_lt));
  Comparator #(.mode("unsigned"), .width(3)) comparator_11 (
    .a(Instruction[14:12]), .b(3'b001), .gt(comparator_11_gt), .eq(comparator_11_eq), .lt(comparator_11_lt));
  Multiplexer #(.select(3), .width(6)) multiplexer_2 (
    .in0(6'b011010), .in1(6'b011011), .in4(6'b011100), .in5(6'b011101), .in6(6'b011110), .in7(6'b011111),
    .out(B11000), .sel(Instruction[14:12]));  // open: in2, in3
  assign bit_extender_1_out = {{4{1'b0}}, priority_encoder_2_out};  // Bit_Extender bit_extender_1
  Priority_Encoder #(.select_enc(2)) priority_encoder_2 (
    .in0(comparator_10_lt), .in1(comparator_10_eq), .in2(comparator_10_gt), .out(priority_encoder_2_out));  // open: in3, gs, en_out, en_in
  Priority_Encoder #(.select_enc(2)) priority_encoder_3 (
    .in0(comparator_11_lt), .in1(comparator_11_eq), .in2(comparator_11_gt), .out(priority_encoder_3_out));  // open: in3, gs, en_out, en_in
  Multiplexer #(.width(6)) multiplexer_3 (
    .in0(6'b010011), .in1(6'b010100), .out(multiplexer_3_out), .sel(comparator_12_eq));
  Comparator #(.mode("unsigned"), .width(7)) comparator_12 (
    .a(Instruction[31:25]), .b({7{1'b0}}), .eq(comparator_12_eq));  // open: gt, lt
  Adder #(.width(6)) adder_1 (.a(bit_extender_1_out), .b(6'b000011), .out(adder_1_out));  // open: cin, cout
  Multiplexer #(.select(2), .width(6)) multiplexer_4 (
    .in0(6'b001000), .in2(6'b001001), .out(multiplexer_4_out), .sel(priority_encoder_2_out));  // open: in1, in3
  assign bit_extender_2_out = {{4{1'b0}}, priority_encoder_3_out};  // Bit_Extender bit_extender_2
  Adder #(.width(6)) adder_2 (.a(bit_extender_2_out), .b(6'b001100), .out(I00000));  // open: cin, cout
  Multiplexer #(.select(3), .width(6)) multiplexer_5 (
    .in0(6'b001111), .in1(6'b010000), .in2(6'b010001), .in4(6'b010010), .in5(multiplexer_3_out),
    .in6(6'b010101), .in7(6'b010110), .out(I00100), .sel(Instruction[14:12]));  // open: in3
  Multiplexer #(.select(3), .width(6)) multiplexer_6 (
    .in0(6'b010111), .in1(6'b011000), .in2(6'b011001), .out(S01000), .sel(Instruction[14:12]));  // open: in3, in4, in5, in6, in7
  Multiplexer #(.select(3), .width(6)) multiplexer_7 (
    .in0(bit_extender_1_out), .in1(adder_1_out), .in2(6'b000110), .in3(6'b000101), .in4(6'b000111),
    .in5(multiplexer_4_out), .in6(6'b001010), .in7(6'b001011), .out(R01100), .sel(Instruction[14:12]));
  Comparator #(.mode("unsigned"), .width(7)) comparator_13 (
    .a(Instruction[6:0]), .b(7'b1100011), .eq(comparator_13_eq));  // open: gt, lt
  Comparator #(.mode("unsigned"), .width(3)) comparator_14 (
    .a(Instruction[14:12]), .b(3'b000), .eq(comparator_14_eq));  // open: gt, lt
  Comparator #(.mode("unsigned"), .width(3)) comparator_15 (
    .a(Instruction[14:12]), .b(3'b001), .eq(comparator_15_eq));  // open: gt, lt
  Comparator #(.mode("unsigned"), .width(3)) comparator_16 (
    .a(Instruction[14:12]), .b(3'b100), .eq(comparator_16_eq));  // open: gt, lt
  Comparator #(.mode("unsigned"), .width(3)) comparator_17 (
    .a(Instruction[14:12]), .b(3'b110), .eq(comparator_17_eq));  // open: gt, lt
  Comparator #(.mode("unsigned"), .width(3)) comparator_18 (
    .a(Instruction[14:12]), .b(3'b101), .eq(comparator_18_eq));  // open: gt, lt
  Comparator #(.mode("unsigned"), .width(3)) comparator_19 (
    .a(Instruction[14:12]), .b(3'b111), .eq(comparator_19_eq));  // open: gt, lt
  Comparator #(.mode("unsigned"), .width(7)) comparator_20 (
    .a(Instruction[6:0]), .b(7'b1100111), .eq(comparator_20_eq));  // open: gt, lt
  Comparator #(.mode("unsigned"), .width(7)) comparator_21 (
    .a(Instruction[6:0]), .b(7'b1101111), .eq(comparator_21_eq));  // open: gt, lt
  not not_1 (not_1_out, BrEq);
  not not_2 (not_2_out, BrLt);
  not not_3 (not_3_out, BrLt);
  and and_1 (and_1_out, comparator_13_eq, comparator_14_eq, BrEq);
  and and_2 (and_2_out, comparator_13_eq, comparator_15_eq, not_1_out);
  and and_3 (and_3_out, comparator_13_eq, comparator_16_eq, BrLt);
  and and_4 (and_4_out, comparator_13_eq, comparator_17_eq, BrLt);
  and and_5 (and_5_out, comparator_13_eq, comparator_18_eq, not_2_out);
  and and_6 (and_6_out, comparator_13_eq, comparator_19_eq, not_3_out);
  or or_1 (or_1_out, and_1_out, and_2_out, and_3_out, and_4_out, and_5_out, and_6_out);
  or or_2 (or_2_out, comparator_20_eq, comparator_21_eq);
  or or_3 (PCSel, or_1_out, or_2_out);

  // Other names for the same wires on the sheet: opcodeCond[6:0] = Instruction[6:0]; opcode[4:0] = Instruction[6:2];
  //   fun3[2:0] = Instruction[14:12]; fun7[6:0] = Instruction[31:25]

  // Notes on the sheet:
  //   INPUTS to your circuit
  //   contents of rom_1 (hex, n*v repeats v):
  //   1001 1401 1601 1081 1481 1581 1101 1201 1281 1681 1301 1381 41 41 41 1041 10cb 1141 1241 12cd 16cb
  //   1341 13c1 842 842 842 4*64 74 74 1067 17c7 2069 2041
  //   ROM FOR CONTROL LOGIC
  //   DON'T CHANGE THE LOCATIONS OF THE INPUTS AND OUTPUTS!
  //   This is only if you choose to do the ROM option
  //   OUTPUT from your circuit
endmodule
