// Logisim project imm-gen.circ as structural Verilog: 1 circuit, main circuit imm_gen
module imm_gen (
  input  [31:0] Instruction,
  input  [2:0] ImmSel,
  output [31:0] Immediate
);

  wire [31:0] bit_extender_1_out, bit_extender_2_out, bit_extender_3_out, bit_extender_4_out,
       bit_extender_5_out, bit_extender_6_out;

  assign bit_extender_1_out = {{20{Instruction[31]}}, Instruction[31:20]};  // Bit_Extender bit_extender_1
  assign bit_extender_2_out = {{20{Instruction[31]}}, {Instruction[31:25], Instruction[11:7]}};  // Bit_Extender bit_extender_2
  assign bit_extender_3_out = {{19{Instruction[31]}}, {Instruction[31], Instruction[7], Instruction[30:25], Instruction[11:8], 1'b0}};  // Bit_Extender bit_extender_3
  assign bit_extender_4_out = {{11{Instruction[31]}}, {Instruction[31], Instruction[19:12], Instruction[20], Instruction[30:21], 1'b0}};  // Bit_Extender bit_extender_4
  assign bit_extender_5_out = {{27{Instruction[24]}}, Instruction[24:20]};  // Bit_Extender bit_extender_5
  assign bit_extender_6_out = {{27{1'b0}}, Instruction[24:20]};  // Bit_Extender bit_extender_6
  Multiplexer #(.select(3), .width(32)) multiplexer_1 (
    .in0(bit_extender_1_out), .in1(bit_extender_2_out), .in2(bit_extender_3_out),
    .in3({Instruction[31:12], {12{1'b0}}}), .in4(bit_extender_4_out), .in5(bit_extender_5_out),
    .in6(bit_extender_6_out), .out(Immediate), .sel(ImmSel));  // open: in7

  // Other names for the same wires on the sheet: I[11:0] = Instruction[31:20]; Ii[4:0] = Instruction[24:20];
  //   J[20:1] = {Instruction[31], Instruction[19:12], Instruction[20], Instruction[30:21]};
  //   U[31:12] = Instruction[31:12];
  //   B[12:1] = {Instruction[31], Instruction[7], Instruction[30:25], Instruction[11:8]};
  //   S[11:0] = {Instruction[31:25], Instruction[11:7]}

  // Notes on the sheet:
  //   INPUTS to your circuit
  //   DON'T CHANGE THE LOCATIONS OF THE INPUTS AND OUTPUTS!
  //   OUTPUT from your circuit
endmodule
