// Logisim project regfile.circ as structural Verilog: 1 circuit, main circuit regfile
module regfile (
  input  [4:0] ReadIndex1,
  input  [4:0] ReadIndex2,
  input  [4:0] WriteIndex,
  input  [31:0] WriteData,
  input  RegWEn,
  input  clk,
  output [31:0] ra,
  output [31:0] sp,
  output [31:0] t0,
  output [31:0] t1,
  output [31:0] t2,
  output [31:0] s0,
  output [31:0] s1,
  output [31:0] a0,
  output [31:0] ReadData1,
  output [31:0] ReadData2
);

  wire wea0, wea1, wea2, wea3, wea4, wea5, wea6, wea7, wegp, wera, wes0, wes1, wes2, wes3, wes4, wes5, wes6,
       wes7, wes8, wes9, wes10, wes11, wesp, wet0, wet1, wet2, wet3, wet4, wet5, wet6, wetp;
  wire [31:0] a1, a2, a3, a4, a5, a6, a7, gp, s2, s3, s4, s5, s6, s7, s8, s9, s10, s11, t3, t4, t5, t6, tp,
       wa0, wa1, wa2, wa3, wa4, wa5, wa6, wa7, wgp, wra, ws0, ws1, ws2, ws3, ws4, ws5, ws6, ws7, ws8, ws9,
       ws10, ws11, wsp, wt0, wt1, wt2, wt3, wt4, wt5, wt6, wtp, x0;

  Register #(.width(32)) register_1 (.D(wra), .en(wera), .clk(clk), .Q(ra));  // open: clr
  Register #(.width(32)) register_2 (.D(wsp), .en(wesp), .clk(clk), .Q(sp));  // open: clr
  Register #(.width(32)) register_3 (.D(wgp), .en(wegp), .clk(clk), .Q(gp));  // open: clr
  Register #(.width(32)) register_4 (.D(wtp), .en(wetp), .clk(clk), .Q(tp));  // open: clr
  Register #(.width(32)) register_5 (.D(wt0), .en(wet0), .clk(clk), .Q(t0));  // open: clr
  Register #(.width(32)) register_6 (.D(wt1), .en(wet1), .clk(clk), .Q(t1));  // open: clr
  Register #(.width(32)) register_7 (.D(wt2), .en(wet2), .clk(clk), .Q(t2));  // open: clr
  Register #(.width(32)) register_8 (.D(ws0), .en(wes0), .clk(clk), .Q(s0));  // open: clr
  Register #(.width(32)) register_9 (.D(ws9), .en(wes9), .clk(clk), .Q(s9));  // open: clr
  Register #(.width(32)) register_10 (.D(wt3), .en(wet3), .clk(clk), .Q(t3));  // open: clr
  Register #(.width(32)) register_11 (.D(ws1), .en(wes1), .clk(clk), .Q(s1));  // open: clr
  Register #(.width(32)) register_12 (.D(wa0), .en(wea0), .clk(clk), .Q(a0));  // open: clr
  Register #(.width(32)) register_13 (.D(wa1), .en(wea1), .clk(clk), .Q(a1));  // open: clr
  Register #(.width(32)) register_14 (.D(wa2), .en(wea2), .clk(clk), .Q(a2));  // open: clr
  Register #(.width(32)) register_15 (.D(wa3), .en(wea3), .clk(clk), .Q(a3));  // open: clr
  Register #(.width(32)) register_16 (.D(wa4), .en(wea4), .clk(clk), .Q(a4));  // open: clr
  Register #(.width(32)) register_17 (.D(wa5), .en(wea5), .clk(clk), .Q(a5));  // open: clr
  Register #(.width(32)) register_18 (.D(wa6), .en(wea6), .clk(clk), .Q(a6));  // open: clr
  Register #(.width(32)) register_19 (.D(ws10), .en(wes10), .clk(clk), .Q(s10));  // open: clr
  Register #(.width(32)) register_20 (.D(wt4), .en(wet4), .clk(clk), .Q(t4));  // open: clr
  Register #(.width(32)) register_21 (.Q(x0));  // open: D, en, clk, clr
  Register #(.width(32)) register_22 (.D(wa7), .en(wea7), .clk(clk), .Q(a7));  // open: clr
  Register #(.width(32)) register_23 (.D(ws2), .en(wes2), .clk(clk), .Q(s2));  // open: clr
  Register #(.width(32)) register_24 (.D(ws3), .en(wes3), .clk(clk), .Q(s3));  // open: clr
  Register #(.width(32)) register_25 (.D(ws4), .en(wes4), .clk(clk), .Q(s4));  // open: clr
  Register #(.width(32)) register_26 (.D(ws5), .en(wes5), .clk(clk), .Q(s5));  // open: clr
  Register #(.width(32)) register_27 (.D(ws6), .en(wes6), .clk(clk), .Q(s6));  // open: clr
  Register #(.width(32)) register_28 (.D(ws7), .en(wes7), .clk(clk), .Q(s7));  // open: clr
  Register #(.width(32)) register_29 (.D(ws8), .en(wes8), .clk(clk), .Q(s8));  // open: clr
  Register #(.width(32)) register_30 (.D(ws11), .en(wes11), .clk(clk), .Q(s11));  // open: clr
  Register #(.width(32)) register_31 (.D(wt5), .en(wet5), .clk(clk), .Q(t5));  // open: clr
  Register #(.width(32)) register_32 (.D(wt6), .en(wet6), .clk(clk), .Q(t6));  // open: clr
  Multiplexer #(.select(5), .width(32)) multiplexer_1 (
    .in0(x0), .in1(ra), .in2(sp), .in3(gp), .in4(tp), .in5(t0), .in6(t1), .in7(t2), .in8(s0), .in9(s1),
    .in10(a0), .in11(a1), .in12(a2), .in13(a3), .in14(a4), .in15(a5), .in16(a6), .in17(a7), .in18(s2),
    .in19(s3), .in20(s4), .in21(s5), .in22(s6), .in23(s7), .in24(s8), .in25(s9), .in26(s10), .in27(s11),
    .in28(t3), .in29(t4), .in30(t5), .in31(t6), .out(ReadData1), .sel(ReadIndex1));
  Multiplexer #(.select(5), .width(32)) multiplexer_2 (
    .in0(x0), .in1(ra), .in2(sp), .in3(gp), .in4(tp), .in5(t0), .in6(t1), .in7(t2), .in8(s0), .in9(s1),
    .in10(a0), .in11(a1), .in12(a2), .in13(a3), .in14(a4), .in15(a5), .in16(a6), .in17(a7), .in18(s2),
    .in19(s3), .in20(s4), .in21(s5), .in22(s6), .in23(s7), .in24(s8), .in25(s9), .in26(s10), .in27(s11),
    .in28(t3), .in29(t4), .in30(t5), .in31(t6), .out(ReadData2), .sel(ReadIndex2));
  Demultiplexer #(.select(5), .width(32)) demultiplexer_1 (
    .out1(wra), .out2(wsp), .out3(wgp), .out4(wtp), .out5(wt0), .out6(wt1), .out7(wt2), .out8(ws0),
    .out9(ws1), .out10(wa0), .out11(wa1), .out12(wa2), .out13(wa3), .out14(wa4), .out15(wa5), .out16(wa6),
    .out17(wa7), .out18(ws2), .out19(ws3), .out20(ws4), .out21(ws5), .out22(ws6), .out23(ws7), .out24(ws8),
    .out25(ws9), .out26(ws10), .out27(ws11), .out28(wt3), .out29(wt4), .out30(wt5), .out31(wt6),
    .in(WriteData), .sel(WriteIndex));  // open: out0
  Demultiplexer #(.select(5)) demultiplexer_2 (
    .out1(wera), .out2(wesp), .out3(wegp), .out4(wetp), .out5(wet0), .out6(wet1), .out7(wet2), .out8(wes0),
    .out9(wes1), .out10(wea0), .out11(wea1), .out12(wea2), .out13(wea3), .out14(wea4), .out15(wea5),
    .out16(wea6), .out17(wea7), .out18(wes2), .out19(wes3), .out20(wes4), .out21(wes5), .out22(wes6),
    .out23(wes7), .out24(wes8), .out25(wes9), .out26(wes10), .out27(wes11), .out28(wet3), .out29(wet4),
    .out30(wet5), .out31(wet6), .in(RegWEn), .sel(WriteIndex));  // open: out0

  // Notes on the sheet:
  //   INPUTS to your circuit
  //   DON'T CHANGE THE LOCATIONS OF THE INPUTS AND OUTPUTS!
  //   These are DEBUG/TEST outputs from your circuit.
  //   OUTPUTS from your circuit
endmodule
